// Digital circuit 2_logic.dig as structural Verilog
module _2_logic (
  input  A,
  input  Clock,
  output Y
);

  wire and_1_out, and_2_out, and_3_out, and_4_out, B_p3, Button_out, nor_1_out, nor_2_out, nor_4_out,
       not_1_out, not_2_out, not_3_out;

  Button Button (.out(Button_out));
  // SwitchDT B: pin names not known; wires that end beside it: Button_out, Clock, B_p3
  not not_1 (not_1_out, A);
  not not_2 (not_2_out, B_p3);
  and and_1 (and_1_out, not_1_out, not_2_out);
  and and_2 (and_2_out, A, not_2_out);
  nor nor_1 (nor_1_out, and_1_out, nor_2_out);
  nor nor_2 (nor_2_out, nor_1_out, and_2_out);
  not not_3 (not_3_out, nor_1_out);
  and and_3 (and_3_out, not_3_out, B_p3);
  and and_4 (and_4_out, nor_1_out, B_p3);
  nor nor_3 (Y, and_3_out, nor_4_out);
  nor nor_4 (nor_4_out, Y, and_4_out);
endmodule
