// Digital circuit 3_block.dig as structural Verilog
module _3_block (
  input  Clock
);

  wire _1i_p3, _2i_p3, _4i_p3, _8i_p3, adder_pin1, adder_pin3, adder_pin4, adder_pin5, adder_pin10,
       adder_pin12, adder_pin13, adder_pin14, B_p3, Clock_out, Reset_p3, Subtract_p3, xor_pin3, xor_pin6,
       xor_pin8, xor_pin11;

  // SwitchDT Subtract: pin names not known; wires that end beside it: 1'b0, 1'b1, Subtract_p3
  // SwitchDT _1i: pin names not known; wires that end beside it: 1'b0, 1'b1, _1i_p3
  // SwitchDT _2i: pin names not known; wires that end beside it: 1'b0, 1'b1, _2i_p3
  // SwitchDT _4i: pin names not known; wires that end beside it: 1'b0, 1'b1, _4i_p3
  // SwitchDT _8i: pin names not known; wires that end beside it: 1'b0, 1'b1, _8i_p3
  // SwitchDT Reset: pin names not known; wires that end beside it: 1'b0, 1'b1, Reset_p3
  _7486 \xor  (
    .pin1(_1i_p3), .pin2(Subtract_p3), .pin3(xor_pin3), .pin4(_2i_p3), .pin5(Subtract_p3), .pin6(xor_pin6),
    .pin7(1'b0), .pin8(xor_pin8), .pin9(_4i_p3), .pin10(Subtract_p3), .pin11(xor_pin11), .pin12(_8i_p3),
    .pin13(Subtract_p3), .pin14(1'b1));
  Button u_Clock (.out(Clock_out));
  // SwitchDT B: pin names not known; wires that end beside it: Clock, Clock_out, B_p3
  _74283 adder (
    .pin1(adder_pin1), .pin2(xor_pin6), .pin3(adder_pin3), .pin4(adder_pin4), .pin5(adder_pin5),
    .pin6(xor_pin3), .pin7(Subtract_p3), .pin8(1'b0), .pin10(adder_pin10), .pin11(xor_pin11),
    .pin12(adder_pin12), .pin13(adder_pin13), .pin14(adder_pin14), .pin15(xor_pin8), .pin16(1'b1));  // open: pin9
  _74173 register (
    .pin1(1'b0), .pin2(1'b0), .pin3(adder_pin5), .pin4(adder_pin3), .pin5(adder_pin14), .pin6(adder_pin12),
    .pin7(B_p3), .pin8(1'b0), .pin9(1'b0), .pin10(1'b0), .pin11(adder_pin10), .pin12(adder_pin13),
    .pin13(adder_pin1), .pin14(adder_pin4), .pin15(Reset_p3), .pin16(1'b1));
  // PolarityAwareLED _1r: pin names not known; wires that end beside it: 1'b0, adder_pin5
  // PolarityAwareLED _2r: pin names not known; wires that end beside it: 1'b0, adder_pin3
  // PolarityAwareLED _4r: pin names not known; wires that end beside it: 1'b0, 1'b0, adder_pin14
  // PolarityAwareLED _8r: pin names not known; wires that end beside it: 1'b0, adder_pin12, 1'b1
endmodule
