// Digital circuit 1b_block.dig as structural Verilog
module _1b_block (
);

  wire _7408_1_pin8, _7408_1_pin11, _7486_1_pin1, _7486_1_pin2, _7486_1_pin4, _7486_1_pin9, _7486_1_pin10,
       _7486_1_pin12, _7486_1_pin13;

  _7486 _7486_1 (
    .pin1(_7486_1_pin1), .pin2(_7486_1_pin2), .pin4(_7486_1_pin4), .pin5(_7486_1_pin4), .pin6(_7486_1_pin4),
    .pin7(_7486_1_pin4), .pin9(_7486_1_pin9), .pin10(_7486_1_pin10), .pin11(_7486_1_pin10),
    .pin12(_7486_1_pin12), .pin13(_7486_1_pin13), .pin14(1'b1));  // open: pin3, pin8
  // SwitchDT A0: pin names not known; wires that end beside it: 1'b1, _7486_1_pin4
  // SwitchDT B0: pin names not known; wires that end beside it: 1'b1, _7486_1_pin4, _7486_1_pin2
  // SwitchDT A1: pin names not known; wires that end beside it: 1'b1, _7486_1_pin4, _7486_1_pin12
  // SwitchDT B1: pin names not known; wires that end beside it: 1'b1, _7486_1_pin4, _7486_1_pin13
  // PolarityAwareLED S0: pin names not known; wires that end beside it: _7486_1_pin4
  // PolarityAwareLED S1: pin names not known; wires that end beside it: _7486_1_pin4
  _7408 _7408_1 (
    .pin1(_7486_1_pin1), .pin2(_7486_1_pin2), .pin3(_7486_1_pin9), .pin4(1'b0), .pin5(1'b0), .pin6(1'b0),
    .pin7(1'b0), .pin8(_7408_1_pin8), .pin9(_7486_1_pin12), .pin10(_7486_1_pin13), .pin11(_7408_1_pin11),
    .pin12(_7486_1_pin10), .pin13(_7486_1_pin9), .pin14(1'b1));
  _7432 _7432_1 (
    .pin1(1'b0), .pin2(1'b0), .pin3(1'b0), .pin4(1'b0), .pin5(1'b0), .pin6(1'b0), .pin7(1'b0), .pin8(1'b0),
    .pin9(1'b0), .pin10(1'b0), .pin12(_7408_1_pin8), .pin13(_7408_1_pin11), .pin14(1'b1));  // open: pin11
  // PolarityAwareLED C: pin names not known; wires that end beside it: 1'b0
endmodule
