// Digital circuit sequentiallogic_recitation.dig as structural Verilog
module sequentiallogic_recitation (
  input  A0,
  input  B0,
  input  A1,
  input  B1,
  output S0,
  output S1,
  output C
);

  wire and_1_out, and_2_out, and_3_out, xor_2_out;

  xor xor_1 (S0, A0, B0);
  and and_1 (and_1_out, B0, A0);
  xor xor_2 (xor_2_out, A1, B1);
  xor xor_3 (S1, and_1_out, xor_2_out);
  and and_2 (and_2_out, xor_2_out, and_1_out);
  and and_3 (and_3_out, A1, B1);
  or or_1 (C, and_2_out, and_3_out);

  // Notes on the sheet:
  //   A0: Input 1
  //   B0: Input 2
endmodule
