// Digital circuit HW1_circuit.dig as structural Verilog
module HW1_circuit (
  input  A,
  input  B,
  input  C,
  output Y
);

  wire and_1_out, and_2_out, or_1_out, or_2_out, or_3_out;

  or or_1 (or_1_out, A, B);
  and and_1 (and_1_out, B, C);
  or or_2 (or_2_out, B, C);
  or or_3 (or_3_out, or_1_out, and_1_out);
  and and_2 (and_2_out, and_1_out, or_2_out);
  xor xor_1 (Y, or_3_out, and_2_out);
endmodule
