// Digital circuit 3input_1output.dig as structural Verilog
module _3input_1output (
  input  A,
  input  B,
  input  C
);

  wire and_1_out, nand_1_out, xor_1_out;

  and and_1 (and_1_out, A, B);
  nand nand_1 (nand_1_out, and_1_out, C);
  xor xor_1 (xor_1_out, nand_1_out, C);
  LED X (.in(nand_1_out));
  LED Y (.in(xor_1_out));
endmodule
