// Digital circuit Lab1a_breadboard.dig as structural Verilog
module Lab1a_breadboard (
);

  wire polarityawareled_1_p2;

  // PolarityAwareLED polarityawareled_1: pin names not known; wires that end beside it: 1'b1, polarityawareled_1_p2, 1'b0
  // SwitchDT switchdt_1: pin names not known; wires that end beside it: polarityawareled_1_p2, 1'b0, 1'b1

  // Notes on the sheet:
  //   Breadboard
endmodule
