// Digital circuit Lab1b_breadboard_template.dig as structural Verilog
module Lab1b_breadboard_template (
);

  wire polarityawareled_1_p1, switchdt_1_p2, switchdt_2_p2, switchdt_3_p2;

  // PolarityAwareLED polarityawareled_1: pin names not known; wires that end beside it: polarityawareled_1_p1, 1'b0
  // SwitchDT switchdt_1: pin names not known; wires that end beside it: polarityawareled_1_p1, switchdt_1_p2
  // SwitchDT switchdt_2: pin names not known; wires that end beside it: switchdt_1_p2, switchdt_2_p2
  // SwitchDT switchdt_3: pin names not known; wires that end beside it: switchdt_2_p2, switchdt_3_p2
  // SwitchDT switchdt_4: pin names not known; wires that end beside it: switchdt_3_p2, 1'b1, 1'b0, 1'b1, 1'b0

  // Notes on the sheet:
  //   Breadboard
endmodule
