// Digital circuit 2b_logic_TEMPLATE.dig as structural Verilog
module _2b_logic_TEMPLATE (
  input  A0,
  input  B0,
  input  A1,
  input  B1
);

  LED S0 ();  // open: in
  LED S1 ();  // open: in
  LED COut ();  // open: in
endmodule
