// Digital circuit 3_breadboard_SOLUTION_DOUBLETHROW.dig as structural Verilog
module _3_breadboard_SOLUTION_DOUBLETHROW (
);

  wire _7402_1_pin3, _7402_1_pin8, _7402_1_pin10, _7404_1_pin1, _7404_1_pin2, _7404_1_pin3, _7404_1_pin4,
       _7404_1_pin5, _7404_1_pin6, _7404_1_pin8, _7408_1_pin3, _7408_1_pin6, _7408_1_pin8, _7408_1_pin11;

  _7404 _7404_1 (
    .pin1(_7404_1_pin1), .pin2(_7404_1_pin2), .pin3(_7404_1_pin3), .pin4(_7404_1_pin4), .pin5(_7404_1_pin5),
    .pin6(_7404_1_pin6), .pin7(1'b0), .pin8(_7404_1_pin8), .pin9(1'b0), .pin10(_7404_1_pin8), .pin11(1'b0),
    .pin12(_7404_1_pin8), .pin13(1'b0), .pin14(1'b1));
  _7408 _7408_1 (
    .pin1(_7404_1_pin2), .pin2(_7404_1_pin4), .pin3(_7408_1_pin3), .pin4(_7404_1_pin1), .pin5(_7404_1_pin4),
    .pin6(_7408_1_pin6), .pin7(1'b0), .pin8(_7408_1_pin8), .pin9(_7404_1_pin5), .pin10(_7404_1_pin3),
    .pin11(_7408_1_pin11), .pin12(_7404_1_pin6), .pin13(_7404_1_pin3), .pin14(1'b1));
  _7402 _7402_1 (
    .pin1(_7404_1_pin5), .pin2(_7408_1_pin3), .pin3(_7402_1_pin3), .pin4(_7402_1_pin3), .pin5(_7408_1_pin6),
    .pin6(_7404_1_pin5), .pin7(1'b0), .pin8(_7402_1_pin8), .pin9(_7408_1_pin8), .pin10(_7402_1_pin10),
    .pin11(_7402_1_pin10), .pin12(_7408_1_pin11), .pin13(_7402_1_pin8), .pin14(1'b1));
  // PolarityAwareLED i: pin names not known; wires that end beside it: 1'b0, _7404_1_pin5
  // PolarityAwareLED Y: pin names not known; wires that end beside it: 1'b0, _7402_1_pin8
  Button Clock (.out(_7404_1_pin3));
  // SwitchDT A: pin names not known; wires that end beside it: _7404_1_pin1, 1'b0, 1'b1, 1'b0, 1'b1, 1'b0, 1'b1

  // Notes on the sheet:
  //   Breadboard
endmodule
