// Digital circuit 3_logic_SOLUTION.dig as structural Verilog
module _3_logic_SOLUTION (
  input  A,
  input  Clock,
  output Y,
  output i
);

  wire and_1_out, and_2_out, and_3_out, and_4_out, nor_2_out, nor_4_out, not_1_out, not_2_out, not_3_out;

  not not_1 (not_1_out, A);
  not not_2 (not_2_out, Clock);
  and and_1 (and_1_out, not_1_out, not_2_out);
  and and_2 (and_2_out, A, not_2_out);
  nor nor_1 (i, and_1_out, nor_2_out);
  nor nor_2 (nor_2_out, i, and_2_out);
  not not_3 (not_3_out, i);
  and and_3 (and_3_out, not_3_out, Clock);
  and and_4 (and_4_out, i, Clock);
  nor nor_3 (Y, and_3_out, nor_4_out);
  nor nor_4 (nor_4_out, Y, and_4_out);
endmodule

/* Test case Tests:
A Clock Y i
0 0 x x
0 1 0 0
0 0 0 0
0 1 0 0
0 0 0 0
1 0 0 1
0 0 0 0
1 0 0 1
1 1 1 1
0 1 1 1
1 1 1 1
1 0 1 1
0 0 1 0
0 1 0 0
0 1 0 0
0 0 0 0
*/
