// Digital circuit NEWFILE.dig as structural Verilog
module NEWFILE (
);

  // _7432 _7432_1: pin names not known
  // _7408 _7408_1: pin names not known
  // _7486 _7486_1: pin names not known
  // PolarityAwareLED COut: pin names not known
  // PolarityAwareLED S1: pin names not known
  // PolarityAwareLED S0: pin names not known
  // SwitchDT A1: pin names not known
  // SwitchDT A0: pin names not known
  // SwitchDT B1: pin names not known
  // SwitchDT B0: pin names not known; wires that end beside it: 1'b0, 1'b1, 1'b0, 1'b1

  // Notes on the sheet:
  //   Breadboard
endmodule
