// Digital circuit Debugging example.dig as structural Verilog
module Debugging_example (
  input  A,
  input  B,
  input  C,
  input  D,
  output Y
);

  wire _7408_1_pin1, _7408_1_pin2, _7408_1_pin3, _7408_1_pin5, _7408_1_pin6, _7408_1_pin8, and_1_out,
       and_2_out, not_1_out, or_1_out, or_2_out, switchdt_1_p3, switchdt_2_p3, switchdt_3_p3, switchdt_4_p3;

  or or_1 (or_1_out, A, B);
  and and_1 (and_1_out, C, D);
  // SwitchDT switchdt_1: pin names not known; wires that end beside it: 1'b1, 1'b0, switchdt_1_p3
  // SwitchDT switchdt_2: pin names not known; wires that end beside it: 1'b1, 1'b0, switchdt_2_p3
  // SwitchDT switchdt_3: pin names not known; wires that end beside it: 1'b1, 1'b0, switchdt_3_p3
  // SwitchDT switchdt_4: pin names not known; wires that end beside it: 1'b1, 1'b0, switchdt_4_p3
  and and_2 (and_2_out, or_1_out, not_1_out);
  not not_1 (not_1_out, and_1_out);
  or or_2 (or_2_out, or_1_out, and_1_out);
  and and_3 (Y, and_2_out, or_2_out);
  _7408 _7408_1 (
    .pin1(_7408_1_pin1), .pin2(_7408_1_pin2), .pin3(_7408_1_pin3), .pin4(_7408_1_pin3), .pin5(_7408_1_pin5),
    .pin6(_7408_1_pin6), .pin7(1'b0), .pin8(_7408_1_pin8), .pin9(switchdt_3_p3), .pin10(switchdt_4_p3),
    .pin11(1'b0), .pin12(1'b0), .pin13(1'b0), .pin14(1'b1));
  _7432 _7432_1 (
    .pin1(1'b0), .pin2(1'b0), .pin3(1'b0), .pin4(switchdt_2_p3), .pin5(switchdt_1_p3), .pin6(_7408_1_pin2),
    .pin7(1'b0), .pin8(_7408_1_pin5), .pin9(_7408_1_pin8), .pin10(_7408_1_pin2), .pin11(1'b0), .pin12(1'b0),
    .pin13(1'b0), .pin14(1'b1));
  LED led_1 (.in(_7408_1_pin6));
  _7404 _7404_1 (
    .pin1(1'b0), .pin2(1'b1), .pin3(1'b0), .pin4(1'b1), .pin5(1'b0), .pin6(1'b1), .pin7(1'b0),
    .pin8(_7408_1_pin1), .pin9(_7408_1_pin8), .pin10(1'b1), .pin11(1'b0), .pin12(1'b1), .pin13(1'b0),
    .pin14(1'b1));
endmodule
