// Digital circuit 2_block.dig as structural Verilog
module _2_block (
  input  Clock
);

  wire A_p3, AND_pin3, AND_pin6, AND_pin8, AND_pin11, B_p3, Button_out, NOR_pin3, NOR_pin8, NOR_pin10,
       NOT_pin2, NOT_pin4, NOT_pin5, NOT_pin6;

  Button Button (.out(Button_out));
  // SwitchDT A: pin names not known; wires that end beside it: 1'b0, 1'b1, A_p3
  // SwitchDT B: pin names not known; wires that end beside it: Button_out, Clock, B_p3
  _7404 NOT (
    .pin1(A_p3), .pin2(NOT_pin2), .pin3(B_p3), .pin4(NOT_pin4), .pin5(NOT_pin5), .pin6(NOT_pin6),
    .pin7(1'b0), .pin9(1'b0), .pin11(1'b0), .pin13(1'b0), .pin14(1'b1));  // open: pin8, pin10, pin12
  _7408 AND (
    .pin1(NOT_pin2), .pin2(NOT_pin4), .pin3(AND_pin3), .pin4(NOT_pin4), .pin5(A_p3), .pin6(AND_pin6),
    .pin7(1'b0), .pin8(AND_pin8), .pin9(NOT_pin5), .pin10(B_p3), .pin11(AND_pin11), .pin12(NOT_pin6),
    .pin13(B_p3), .pin14(1'b1));
  _7402 NOR (
    .pin1(NOT_pin5), .pin2(AND_pin3), .pin3(NOR_pin3), .pin4(NOR_pin3), .pin5(NOT_pin5), .pin6(AND_pin6),
    .pin7(1'b0), .pin8(NOR_pin8), .pin9(AND_pin8), .pin10(NOR_pin10), .pin11(NOR_pin10), .pin12(AND_pin11),
    .pin13(NOR_pin8), .pin14(1'b1));
  // PolarityAwareLED i: pin names not known; wires that end beside it: 1'b0, NOT_pin5
  // PolarityAwareLED Y: pin names not known; wires that end beside it: 1'b0, NOR_pin8
endmodule
