// Digital circuit 1a_block.dig as structural Verilog
module _1a_block (
);

  wire _7408_1_pin3, A_p2, A_p3, B_p3, C_p3;

  // SwitchDT A: pin names not known; wires that end beside it: 1'b1, A_p2, A_p3
  // SwitchDT B: pin names not known; wires that end beside it: 1'b1, A_p2, B_p3
  // SwitchDT C: pin names not known; wires that end beside it: A_p3, A_p2, C_p3
  _7408 _7408_1 (
    .pin1(C_p3), .pin2(B_p3), .pin3(_7408_1_pin3), .pin4(A_p2), .pin5(A_p2), .pin6(A_p2), .pin7(A_p2),
    .pin8(A_p2), .pin9(A_p2), .pin10(A_p2), .pin11(A_p2), .pin12(A_p2), .pin13(A_p2), .pin14(1'b1));
  // PolarityAwareLED Y: pin names not known; wires that end beside it: _7408_1_pin3, A_p2, 1'b0
endmodule
